// Logisim project project1.circ as structural Verilog: 19 circuits, main circuit XORGate
module XORGate (
  input  x,
  input  y,
  output out_3
);

  wire and_1_out, and_2_out, not_1_out, not_2_out;

  not not_1 (not_1_out, x);
  not not_2 (not_2_out, y);
  and and_1 (and_1_out, not_1_out, y);
  and and_2 (and_2_out, x, not_2_out);
  or or_1 (out_3, and_1_out, and_2_out);

  // Notes on the sheet:
  //   XOR Circuit Logisim
endmodule

module OneBitAdd (
  input  A,
  input  B,
  input  Cin,
  output S,
  output COut
);

  wire and_1_out, and_2_out, xor_1_out;

  xor xor_1 (xor_1_out, A, B);
  and and_1 (and_1_out, xor_1_out, Cin);
  and and_2 (and_2_out, A, B);
  xor xor_2 (S, xor_1_out, Cin);
  or or_1 (COut, and_1_out, and_2_out);

  // Notes on the sheet:
  //   A
  //   B
  //   C in
  //   1 Bit Adder
  //   C out
  //   S
endmodule

module FourBitAdd (
  input  [3:0] B,
  input  [3:0] A,
  input  Cin,
  output COut,
  output V,
  output [3:0] S
);

  wire onebitadd_1_cout, onebitadd_2_cout;

  OneBitAdd onebitadd_1 (.A(A[0]), .B(B[0]), .Cin(Cin), .S(S[0]), .COut(onebitadd_1_cout));
  OneBitAdd onebitadd_2 (.A(A[1]), .B(B[1]), .Cin(onebitadd_1_cout), .S(S[1]), .COut(onebitadd_2_cout));
  OneBitAdd onebitadd_3 (.A(A[2]), .B(B[2]), .Cin(onebitadd_2_cout), .S(S[2]), .COut(V));
  OneBitAdd onebitadd_4 (.A(A[3]), .B(B[3]), .Cin(V), .S(S[3]), .COut(COut));

  // Notes on the sheet:
  //   4 Bit Adder
endmodule

module EightBitAdd (
  input  [7:0] A,
  input  [7:0] B,
  input  Cin,
  output COut,
  output V,
  output [7:0] S
);

  wire fourbitadd_1_cout;

  FourBitAdd fourbitadd_1 (.B(B[3:0]), .A(A[3:0]), .Cin(Cin), .COut(fourbitadd_1_cout), .S(S[3:0]));  // open: V
  FourBitAdd fourbitadd_2 (.B(B[7:4]), .A(A[7:4]), .Cin(fourbitadd_1_cout), .COut(COut), .V(V), .S(S[7:4]));
endmodule

module SixteenBitAdd (
  input  [15:0] A,
  input  [15:0] B,
  input  Cin,
  output COut,
  output V,
  output [15:0] S
);

  wire eightbitadd_1_cout;

  EightBitAdd eightbitadd_1 (.A(A[7:0]), .B(B[7:0]), .Cin(Cin), .COut(eightbitadd_1_cout), .S(S[7:0]));  // open: V
  EightBitAdd eightbitadd_2 (.A(A[15:8]), .B(B[15:8]), .Cin(eightbitadd_1_cout), .COut(COut), .V(V), .S(S[15:8]));
endmodule

module ThirtyTwoBidAdd (
  input  [31:0] A,
  input  [31:0] B,
  input  Cin,
  output overflow,
  output [31:0] S
);

  wire sixteenbitadd_1_cout, sixteenbitadd_2_cout, sixteenbitadd_2_v;

  SixteenBitAdd sixteenbitadd_1 (
    .A(A[15:0]), .B(B[15:0]), .Cin(Cin), .COut(sixteenbitadd_1_cout), .S(S[15:0]));  // open: V
  SixteenBitAdd sixteenbitadd_2 (
    .A(A[31:16]), .B(B[31:16]), .Cin(sixteenbitadd_1_cout), .COut(sixteenbitadd_2_cout),
    .V(sixteenbitadd_2_v), .S(S[31:16]));
  xor xor_1 (overflow, sixteenbitadd_2_cout, sixteenbitadd_2_v);
endmodule

module LeftShift32 (
  input  [31:0] B,
  input  [4:0] Sa,
  input  Cin,
  output [31:0] C
);

  SixteenBitShift sixteenbitshift_1 (.Sa(Sa), .B(B), .Cin(Cin), .C(C));

  // Notes on the sheet:
  //   Do not delete or rename any of the input or output pins, and do not add any other pins.
  //   (It's fine to move them around, though)
endmodule

module Add32 (
  input  [31:0] A,
  input  [31:0] B,
  input  Cin,
  output [31:0] C,
  output V
);

  ThirtyTwoBidAdd thirtytwobidadd_1 (.A(A), .B(B), .Cin(Cin), .overflow(V), .S(C));

  // Notes on the sheet:
  //   Do not delete or rename any of the input or output pins, and do not add any other pins.
  //   (It's fine to move the pins around, though)
endmodule

module ALU32 (
  input  [31:0] A,
  input  [31:0] B,
  input  [3:0] Op,
  input  [4:0] Sa,
  output [31:0] C,
  output V
);

  wire [31:0] addsubtract_1_c, compareoperation_1_cout, logicoperation_1_c, shiftop_1_c;

  LogicOperation logicoperation_1 (.A(A), .B(B), .Op(Op), .C(logicoperation_1_c));
  CompareOperation compareoperation_1 (.A(A), .B(B), .Op(Op), .Cout(compareoperation_1_cout));
  ShiftOp shiftop_1 (.B(B), .Op(Op), .Sa(Sa), .C(shiftop_1_c));
  AddSubtract addsubtract_1 (.A(A), .B(B), .Op(Op), .C(addsubtract_1_c), .V(V));
  assign C = logicoperation_1_c | compareoperation_1_cout | shiftop_1_c | addsubtract_1_c;  // OR_Gate or_1, 32 bits wide

  // Notes on the sheet:
  //   Do not delete or rename any of the input or output pins, and do not add any other pins.
  //   (It's fine to move the pins around, though)
endmodule

module OneBitShift (
  input  [4:0] Sa,
  input  [31:0] B,
  input  Cin,
  output [31:0] C
);

  Multiplexer #(.width(32), .enable("false")) multiplexer_1 (.in0(B), .in1({B[30:0], Cin}), .out(C), .sel(Sa[0]));

  // Notes on the sheet:
  //   One Bit Shifter
endmodule

module TwoBitShift (
  input  [4:0] Sa,
  input  [31:0] B,
  input  Cin,
  output [31:0] C
);

  wire [31:0] multiplexer_1_out, onebitshift_1_c;

  Multiplexer #(.width(32), .enable("false")) multiplexer_1 (
    .in0(B), .in1({B[29:0], {2{Cin}}}), .out(multiplexer_1_out), .sel(Sa[1]));
  OneBitShift onebitshift_1 (.Sa(Sa), .B(multiplexer_1_out), .Cin(Cin), .C(onebitshift_1_c));
  Multiplexer #(.width(32), .enable("false")) multiplexer_2 (
    .in0(multiplexer_1_out), .in1(onebitshift_1_c), .out(C), .sel(Sa[0]));
endmodule

module FourBitShift (
  input  [4:0] Sa,
  input  [31:0] B,
  input  Cin,
  output [31:0] C
);

  wire or_1_out;
  wire [31:0] multiplexer_1_out, twobitshift_1_c;

  or or_1 (or_1_out, Sa[0], Sa[1]);
  Multiplexer #(.width(32), .enable("false")) multiplexer_1 (
    .in0(B), .in1({B[27:0], {4{Cin}}}), .out(multiplexer_1_out), .sel(Sa[2]));
  TwoBitShift twobitshift_1 (.Sa(Sa), .B(multiplexer_1_out), .Cin(Cin), .C(twobitshift_1_c));
  Multiplexer #(.width(32), .enable("false")) multiplexer_2 (
    .in0(multiplexer_1_out), .in1(twobitshift_1_c), .out(C), .sel(or_1_out));
endmodule

module EightBitShift (
  input  [4:0] Sa,
  input  [31:0] B,
  input  Cin,
  output [31:0] C
);

  wire or_1_out;
  wire [31:0] fourbitshift_1_c, multiplexer_1_out;

  or or_1 (or_1_out, Sa[0], Sa[1], Sa[2]);
  Multiplexer #(.width(32), .enable("false")) multiplexer_1 (
    .in0(B), .in1({B[23:0], {8{Cin}}}), .out(multiplexer_1_out), .sel(Sa[3]));
  FourBitShift fourbitshift_1 (.Sa(Sa), .B(multiplexer_1_out), .Cin(Cin), .C(fourbitshift_1_c));
  Multiplexer #(.width(32), .enable("false")) multiplexer_2 (
    .in0(multiplexer_1_out), .in1(fourbitshift_1_c), .out(C), .sel(or_1_out));
endmodule

module SixteenBitShift (
  input  [4:0] Sa,
  input  [31:0] B,
  input  Cin,
  output [31:0] C
);

  wire or_1_out;
  wire [31:0] eightbitshift_1_c, multiplexer_1_out;

  or or_1 (or_1_out, Sa[0], Sa[1], Sa[2], Sa[3]);
  Multiplexer #(.width(32), .enable("false")) multiplexer_1 (
    .in0(B), .in1({B[15:0], {16{Cin}}}), .out(multiplexer_1_out), .sel(Sa[4]));
  Multiplexer #(.width(32), .enable("false")) multiplexer_2 (
    .in0(multiplexer_1_out), .in1(eightbitshift_1_c), .out(C), .sel(or_1_out));
  EightBitShift eightbitshift_1 (.Sa(Sa), .B(multiplexer_1_out), .Cin(Cin), .C(eightbitshift_1_c));
endmodule

module LogicOperation (
  input  [31:0] A,
  input  [31:0] B,
  input  [3:0] Op,
  output [31:0] C
);

  wire aand_out, exor_out, nnor_out, not_1_out, not_2_out, not_3_out, not_4_out, not_5_out, not_6_out,
       not_7_out, not_8_out, oor_out, or_2_out;
  wire [31:0] and_1_out, nor_1_out, or_1_out, xor_1_out;

  assign nor_1_out = ~(A | B);  // NOR_Gate nor_1, 32 bits wide
  assign xor_1_out = A ^ B;  // XOR_Gate xor_1, 32 bits wide
  assign and_1_out = A & B;  // AND_Gate and_1, 32 bits wide
  assign or_1_out = A | B;  // OR_Gate or_1, 32 bits wide
  not not_1 (not_1_out, Op[0]);
  not not_2 (not_2_out, Op[3]);
  not not_3 (not_3_out, Op[1]);
  not not_4 (not_4_out, Op[2]);
  Multiplexer #(.select(2), .width(32)) multiplexer_1 (
    .in0(xor_1_out), .in1(nor_1_out), .in2(or_1_out), .in3(and_1_out), .out(C), .sel({Op[3], Op[0]}),
    .en(or_2_out));
  and exor (exor_out, not_1_out, Op[1], Op[2], not_2_out);
  and nnor (nnor_out, Op[0], Op[1], Op[2], not_5_out);
  not not_5 (not_5_out, Op[3]);
  and aand (aand_out, Op[0], not_3_out, not_4_out, Op[3]);
  not not_6 (not_6_out, Op[0]);
  not not_7 (not_7_out, Op[1]);
  not not_8 (not_8_out, Op[2]);
  or or_2 (or_2_out, exor_out, nnor_out, aand_out, oor_out);
  and oor (oor_out, not_6_out, not_7_out, not_8_out, Op[3]);

  // Notes on the sheet:
  //   0110 = XOr
  //   0111 = Nor
  //   1001 = AND
  //   1000 = OR
endmodule

module CompareOperation (
  input  [31:0] A,
  input  [31:0] B,
  input  [3:0] Op,
  output [31:0] Cout
);

  wire and_4_out, and_6_out, and_7_out, eq_out, gt_out, le_out, ne_out, not_2_out, not_3_out, not_4_out,
       not_5_out, not_6_out, not_7_out, not_8_out, not_9_out, not_10_out, not_11_out, not_12_out, not_13_out,
       not_14_out, not_15_out, or_1_out;
  wire [1:0] and_2_out, and_5_out;
  wire [7:0] and_1_out, and_3_out;
  wire [31:0] bit_extender_1_out, bit_extender_2_out, bit_extender_3_out, bit_extender_4_out, not_1_out,
       xnor_1_out;

  assign not_1_out = ~A;  // NOT_Gate not_1, 32 bits wide
  assign xnor_1_out = ~(A ^ B);  // XNOR_Gate xnor_1, 32 bits wide
  assign and_1_out = not_1_out[7:0] & not_1_out[15:8] & not_1_out[23:16] & not_1_out[31:24];  // AND_Gate and_1, 8 bits wide
  not not_2 (not_2_out, Op[0]);
  and le (le_out, not_2_out, Op[1], not_3_out, not_4_out);
  not not_3 (not_3_out, Op[2]);
  not not_4 (not_4_out, Op[3]);
  and gt (gt_out, Op[0], Op[1], not_5_out, not_6_out);
  not not_5 (not_5_out, Op[2]);
  not not_6 (not_6_out, Op[3]);
  not not_7 (not_7_out, Op[0]);
  not not_8 (not_8_out, Op[1]);
  and ne (ne_out, not_7_out, not_8_out, Op[2], not_9_out);
  not not_9 (not_9_out, Op[3]);
  not not_10 (not_10_out, Op[1]);
  and eq (eq_out, Op[0], not_10_out, Op[2], not_11_out);
  not not_11 (not_11_out, Op[3]);
  assign and_2_out = and_1_out[1:0] & and_1_out[3:2] & and_1_out[5:4] & and_1_out[7:6];  // AND_Gate and_2, 2 bits wide
  assign and_3_out = xnor_1_out[7:0] & xnor_1_out[15:8] & xnor_1_out[23:16] & xnor_1_out[31:24];  // AND_Gate and_3, 8 bits wide
  not not_12 (not_12_out, A[31]);
  and and_4 (and_4_out, and_2_out[0], and_2_out[1]);
  assign and_5_out = and_3_out[1:0] & and_3_out[3:2] & and_3_out[5:4] & and_3_out[7:6];  // AND_Gate and_5, 2 bits wide
  not not_13 (not_13_out, and_4_out);
  and and_6 (and_6_out, and_5_out[0], and_5_out[1]);
  and and_7 (and_7_out, not_13_out, not_12_out);
  or or_1 (or_1_out, le_out, gt_out, ne_out, eq_out);
  assign bit_extender_1_out = {{31{1'b0}}, not_14_out};  // Bit_Extender bit_extender_1
  assign bit_extender_2_out = {{31{1'b0}}, and_6_out};  // Bit_Extender bit_extender_2
  not not_14 (not_14_out, and_6_out);
  not not_15 (not_15_out, and_7_out);
  Multiplexer #(.select(2), .width(32)) multiplexer_1 (
    .in0(bit_extender_1_out), .in1(bit_extender_2_out), .in2(bit_extender_3_out), .in3(bit_extender_4_out),
    .out(Cout), .sel(Op[1:0]), .en(or_1_out));
  assign bit_extender_3_out = {{31{1'b0}}, not_15_out};  // Bit_Extender bit_extender_3
  assign bit_extender_4_out = {{31{1'b0}}, and_7_out};  // Bit_Extender bit_extender_4

  // Notes on the sheet:
  //   0010 - le
  //   0011 - gt
  //   0100 - ne
  //   0101 - eq
endmodule

module MirrorCirc (
  input  [31:0] B,
  output [31:0] BMirror,
  output SignBit
);


  assign BMirror = {B[0], B[1], B[2], B[3], B[4], B[5], B[6], B[7], B[8], B[9], B[10], B[11], B[12], B[13], B[14], B[15], B[16], B[17], B[18], B[19], B[20], B[21], B[22], B[23], B[24], B[25], B[26], B[27], B[28], B[29], B[30], B[31]};
  assign SignBit = B[31];
endmodule

module ShiftOp (
  input  [31:0] B,
  input  [3:0] Op,
  input  [4:0] Sa,
  output [31:0] C
);

  wire and_1_out, and_2_out, and_3_out, and_4_out, mirrorcirc_1_signbit, not_1_out, not_2_out, not_3_out,
       not_4_out, not_5_out, or_1_out;
  wire [4:0] and_5_out, bit_extender_1_out;
  wire [31:0] mirrorcirc_1_bmirror, mirrorcirc_2_bmirror, multiplexer_1_out, sixteenbitshift_1_c;

  not not_1 (not_1_out, Op[1]);
  not not_2 (not_2_out, Op[2]);
  not not_3 (not_3_out, Op[3]);
  not not_4 (not_4_out, Op[1]);
  MirrorCirc mirrorcirc_1 (.B(B), .BMirror(mirrorcirc_1_bmirror), .SignBit(mirrorcirc_1_signbit));
  Multiplexer #(.width(32)) multiplexer_1 (
    .in0(mirrorcirc_1_bmirror), .in1(B), .out(multiplexer_1_out), .sel(Op[3]), .en(or_1_out));
  and and_1 (and_1_out, not_1_out, not_2_out, not_3_out);
  and and_2 (and_2_out, not_4_out, Op[2], Op[3]);
  and and_3 (and_3_out, mirrorcirc_1_signbit, Op[0]);
  or or_1 (or_1_out, and_1_out, and_2_out);
  assign bit_extender_1_out = {{4{or_1_out}}, or_1_out};  // Bit_Extender bit_extender_1
  and and_4 (and_4_out, and_3_out, not_5_out);
  not not_5 (not_5_out, Op[3]);
  assign and_5_out = bit_extender_1_out & Sa;  // AND_Gate and_5, 5 bits wide
  SixteenBitShift sixteenbitshift_1 (.Sa(and_5_out), .B(multiplexer_1_out), .Cin(and_4_out), .C(sixteenbitshift_1_c));
  MirrorCirc mirrorcirc_2 (.B(sixteenbitshift_1_c), .BMirror(mirrorcirc_2_bmirror));  // open: SignBit
  Multiplexer #(.width(32)) multiplexer_2 (
    .in0(mirrorcirc_2_bmirror), .in1(sixteenbitshift_1_c), .out(C), .sel(Op[3]), .en(or_1_out));
endmodule

module AddSubtract (
  input  [31:0] A,
  input  [31:0] B,
  input  [3:0] Op,
  output [31:0] C,
  output V
);

  wire AddOp_out, not_2_out, or_1_out, SubtractOp_out;
  wire [31:0] multiplexer_1_out, multiplexer_2_out, not_1_out;

  Multiplexer #(.width(32)) multiplexer_1 (.in0(A), .in1(A), .out(multiplexer_1_out), .sel(Op[3]), .en(or_1_out));
  assign not_1_out = ~B;  // NOT_Gate not_1, 32 bits wide
  not not_2 (not_2_out, Op[2]);
  and AddOp (AddOp_out, Op[1], not_2_out, Op[3]);
  and SubtractOp (SubtractOp_out, Op[1], Op[2], Op[3]);
  Multiplexer #(.width(32)) multiplexer_2 (
    .in0(B), .in1(not_1_out), .out(multiplexer_2_out), .sel(Op[2]), .en(or_1_out));
  or or_1 (or_1_out, AddOp_out, SubtractOp_out);
  ThirtyTwoBidAdd thirtytwobidadd_1 (
    .A(multiplexer_1_out), .B(multiplexer_2_out), .Cin(SubtractOp_out), .overflow(V), .S(C));

  // Notes on the sheet:
  //   Subtract = 111X
  //   Add = 101X
endmodule
